# Fritzing sketch LCD_st7920_128_64 (saved by Fritzing 0.9.3b)
breadboards: 1

parts:
  Componente1 = Arduino Uno (Rev3)
  GLCD_128x1 = 128 x 64 Graphic LCD
  R1 = TRIMPOT [package=trimpot_pth_s3_lock]

nets:
  N1: Componente1.D4, GLCD_128x1.4_D/I
  N2: Componente1.D5_PWM, GLCD_128x1.5_R/W
  N3: Componente1.D6_PWM, GLCD_128x1.6_Enable
  N4: Componente1.D7, GLCD_128x1.17_RST
  N5: Componente1.5V, R1.CCW
  N6: Componente1.GND, R1.CW

notes:
  4
  5
  6
  7
  N.A.V.E-tech - UNIR_Samsung da Amazonia
  Universal 8bit Graphics - U8GLIB
  ST7920_128X64
