# Fritzing sketch eeprom (saved by Fritzing 0.9.3b)
breadboards: 1

parts:
  Componente1 = Arduino Uno (Rev3)
  U1 = TMP01 - Low Power, Programmable Temperature Controller [part_number=TMP01]
  R1 = Resistor [tolerance=±5% resistance=10k package="0603 [SMD]"]

nets:
  N1: Componente1.A4/SDA, U1.10V, R1.Pin_1
  N2: Componente1.A5/SCL, U1.5V
  N3: U1.2p5V, U1.V+
  N4: U1.COMMON, R1.Pin_0

notes:
  EEPROM 24LC256
