# Fritzing sketch esp8266_lowPower (saved by Fritzing 0.9.3b)
breadboards: 1

parts:
  R1 = Resistor [tolerance=±5% resistance=10k package=THT]  # not connected
  R2 = Resistor [tolerance=±5% resistance=10k package=THT]  # not connected
  LED1 = LED - 3mm [color="Red (633nm)" package="3 mm [THT]"]
  R3 = Resistor [tolerance=±5% resistance=10k package=THT]
  U1 = ESP8266 WiFi Module [part_number=ESP8266]  # not connected
  Componente1 = Arduino Uno (Rev3)
  R4 = Resistor [tolerance=±5% resistance=10k package=THT]
  R5 = Resistor [tolerance=±5% resistance=1k package=THT]

nets:
  N1: LED1.anode, R3.Pin_0
  N2: R3.Pin_1, Componente1.5V, R4.Pin_0, R5.Pin_0
  N3: Componente1.RESET, Componente1.GND

notes:
  PULSE GND TO PROGRAM (Compiler Time)
  GND TO PROGRAM and FLOATING to run
  Optimizing Power Consumption on ESP8266
