# Fritzing sketch melex_thermo (saved by Fritzing 0.9.3b)
breadboards: 1

parts:
  Componente1 = Arduino Uno (Rev3)
  Lhi1 = LHi958 [package=to-39]
  R1 = Resistor [tolerance=±5% resistance=4.7k package=THT]
  R2 = Resistor [tolerance=±5% resistance=4.7k package=THT]
  R3 = Resistor [tolerance=±5% resistance=220 package=THT]
  LED1 = LED - 3mm [color="Red (633nm)" package="3 mm [THT]"]
  C1 = Capacitor [part_number=104 package=cap-pth-small2]

nets:
  N1: Componente1.A4/SDA, R2.Pin_1
  N2: Componente1.A5/SCL, Lhi1.GND, R1.Pin_0
  N3: Componente1.D8, LED1.anode
  N4: Componente1.3V3, R1.Pin_1, R2.Pin_0, R3.Pin_1, C1.2
  N5: Componente1.GND, Lhi1.D, C1.1
  N6: R3.Pin_0, LED1.cathode
