# Fritzing sketch pirSensor (saved by Fritzing 0.9.3b)

parts:
  R1 = Resistor [tolerance=±5% resistance=320 package=THT]
  Componente1 = Arduino Uno (Rev3)
  U1 = MLX90614 [package=to-39]
  LED1 = LED - 3mm [color="Red (633nm)" package="3 mm [THT]"]

nets:
  N1: R1.Pin_0, Componente1.GND, U1.SCL_VZ, LED1.anode
  N2: R1.Pin_1, Componente1.A5/SCL, LED1.cathode
  N3: Componente1.D2, U1.PWM_SDA

notes:
  PIR Motion Sensing LED Display
  <module fritzingVersion="0.9.3b.04.19.5c895d327c44a3114e5fcc9d8260daf0cbb52806">
   <boundingRects>
    <boundingRect name="Visão Esquemático" rect="0 0 0 0"/>
    <boundingRect name="Visão Protoboard" rect="-260.073 -173.846 783 11.7"/>
    <boundingRect name="Visão PCB" rect="0 0 0 0"/>
   </boundingRects>
   <instances>
    <instance moduleIdRef="BreadboardLogoTextModuleID" path=":/resources/parts/core/breadboardlogotext.fzp" modelIndex="85416774">
     <property name="logo" value="PIR Motion Sensing LED Display&#xa;Building a PIR Sensor-Based Motion Detector with Arduino"/>
     <property name="color" value="#787878"/>
     <property name="width" value="220.98000000000002"/>
     <property name="height" value="3.302"/>
     <property name="shape" value="&lt;svg viewBox=&quot;0 0 870 13&quot; height=&quot;.13in&quot; xmlns=&quot;http://www.w3.org/2000/svg&quot; width=&quot;8.7in&quot;>&#xa; &lt;g id=&quot;breadboard&quot;>&#xa;  &lt;text font-size=&quot;10&quot; stroke-width=&quot;0&quot; id=&quot;label&quot; xml:space=&quot;preserve&quot; fill=&quot;#787878&quot; font-family=&quot;Droid Sans&quot; x=&quot;435&quot; text-anchor=&quot;middle&quot; y=&quot;9&quot;>PIR Motion Sensing LED Display&#xa;Building a PIR Sensor-Based Motion Detector with Arduino&lt;/text>&#xa; &lt;/g>&#xa;&lt;/svg>&#xa;"/>
     <property name="lastfilename" value=":/resources/parts/svg/core/breadboard/breadboardlogo.svg"/>
     <title>TXT1</title>
     <views>
      <breadboardView layer="breadboard">
       <geometry z="2.50004" x="-260.073" y="-173.846"/>
      </breadboardView>
      <schematicView layer="">
       <geometry z="0" x="791.555" y="273.842"/>
      </schematicView>
      <pcbView layer="">
       <geometry z="0" x="50" y="71.587"/>
      </pcbView>
     </views>
    </instance>
   </instances>
  </module>
  Building a PIR Sensor-Based Motion Detector with Arduino
