# Fritzing sketch rain_v1 (saved by Fritzing 0.9.3b)
breadboards: 1

parts:
  Componente1 = Arduino Uno (Rev3)
  LED1 = LED - 3mm [color="Red (633nm)" package="3 mm [THT]"]
  LED2 = LED - 3mm [color="Green (555nm)" package="3 mm [THT]"]
  R1 = Resistor [tolerance=±5% resistance=330 package=THT]
  R2 = Resistor [tolerance=±5% resistance=330 package=THT]
  R3 = Resistor [tolerance=±5% resistance=330 package=THT]  # not connected

nets:
  N1: Componente1.D6_PWM, LED2.anode
  N2: Componente1.D7, LED1.anode
  N3: LED1.cathode, R1.Pin_0
  N4: LED2.cathode, R2.Pin_0
  N5: R1.Pin_1, R2.Pin_1

notes:
  vcc
  GND
  A0
