# Fritzing sketch Liquid_water_level_sensor_v1 (saved by Fritzing 0.9.3b)
breadboards: 1

parts:
  Componente1 = Arduino Uno (Rev3)
  R1 = Resistor [tolerance=±5% resistance=220 package="0603 [SMD]"]
  S1 = Reed switch [part_number="reed switch" package=THT]
  R2 = Resistor [tolerance=±5% resistance=10k package="0603 [SMD]"]
  LED1 = LED - 3mm [color="Green (555nm)" package="3 mm [THT]"]

nets:
  N1: Componente1.D2, R1.Pin_1
  N2: Componente1.D3_PWM, S1.pin_1, R2.Pin_1
  N3: Componente1.5V, S1.pin_2
  N4: Componente1.GND, R2.Pin_0, LED1.cathode
  N5: R1.Pin_0, LED1.anode

notes:
  22_UNIR_liquid_water_level_sensor_v1
  N.A.V.E-tech - UNIR_Samsung da Amazonia
