# Fritzing sketch xbee_doorbel_system (saved by Fritzing 0.9.3b)

parts:
  Componente1 = Arduino XBee Shield
  U2 = XBEE-1 [package=xbee-silk]  # not connected
  Componente3 = Arduino XBee Shield
  U3 = XBEE-1 [package=xbee-silk]  # not connected
  Componente4 = Max Power IR LED Kit
  Componente5 = Max Power IR LED Kit
  Componente6 = Max Power IR LED Kit

nets:
  N1: Componente1.A2, Componente6.VCC
  N2: Componente1.A4, Componente6.CONTROL
  N3: Componente1.UART_TX, Componente6.GND
  N4: Componente3.D8, Componente5.VCC
  N5: Componente3.D9, Componente4.CONTROL
  N6: Componente3.D10, Componente4.VCC
  GND: Componente3.GND, Componente4.GND, Componente5.GND

notes:
  XBee Receiver Station
  XBee Transmiter Station
  RGB
  Buzzer
  Push But
  N.A.V.E-TECH-UNIR-Samsung-da-Amazonia
  DoorBell Project - XBee Radios
